// Logisim project 全加器.circ as structural Verilog: 3 circuits, main circuit main
module main (
  input  in_1,
  input  in_2,
  input  in_3,
  input  in_4,
  input  in_5,
  input  in_6,
  input  in_7,
  input  in_8,
  input  sub,
  input  in_10,
  input  in_11,
  input  in_12,
  input  in_13,
  input  in_14,
  input  in_15,
  input  in_16,
  input  in_17,
  output out_18,
  output out_19,
  output out_20,
  output out_21,
  output out_22,
  output out_23,
  output out_24,
  output out_25,
  output cout,
  output of
);

  wire \一位进位加法器_1_p4 , \一位进位加法器_1_p5 , \一位进位加法器_2_p4 , \一位进位加法器_2_p5 , \一位进位加法器_3_p4 , \一位进位加法器_3_p5 ,
       \一位进位加法器_4_p4 , \一位进位加法器_4_p5 , \一位进位加法器_5_p4 , \一位进位加法器_5_p5 , \一位进位加法器_6_p4 , \一位进位加法器_6_p5 ,
       \一位进位加法器_7_p4 , \一位进位加法器_7_p5 , \一位进位加法器_8_p4 ;

  xor xor_1 (of, \一位进位加法器_1_p5 , cout);
  // 一位进位加法器 一位进位加法器_1: pin names not known; wires that end beside it: cout, in_10, out_18, \一位进位加法器_1_p4 , \一位进位加法器_1_p5 
  xor xor_2 (\一位进位加法器_1_p4 , in_1, sub);
  // 一位进位加法器 一位进位加法器_2: pin names not known; wires that end beside it: \一位进位加法器_1_p5 , in_11, out_19, \一位进位加法器_2_p4 , \一位进位加法器_2_p5 
  xor xor_3 (\一位进位加法器_2_p4 , in_2, sub);
  // 一位进位加法器 一位进位加法器_3: pin names not known; wires that end beside it: \一位进位加法器_2_p5 , in_12, out_20, \一位进位加法器_3_p4 , \一位进位加法器_3_p5 
  xor xor_4 (\一位进位加法器_3_p4 , in_3, sub);
  // 一位进位加法器 一位进位加法器_4: pin names not known; wires that end beside it: \一位进位加法器_3_p5 , in_13, out_21, \一位进位加法器_4_p4 , \一位进位加法器_4_p5 
  xor xor_5 (\一位进位加法器_4_p4 , in_4, sub);
  // 一位进位加法器 一位进位加法器_5: pin names not known; wires that end beside it: \一位进位加法器_4_p5 , in_14, out_22, \一位进位加法器_5_p4 , \一位进位加法器_5_p5 
  // 一位进位加法器 一位进位加法器_6: pin names not known; wires that end beside it: \一位进位加法器_5_p5 , in_15, out_23, \一位进位加法器_6_p4 , \一位进位加法器_6_p5 
  xor xor_6 (\一位进位加法器_5_p4 , in_5, sub);
  // 一位进位加法器 一位进位加法器_7: pin names not known; wires that end beside it: \一位进位加法器_6_p5 , in_16, out_24, \一位进位加法器_7_p4 , \一位进位加法器_7_p5 
  xor xor_7 (\一位进位加法器_6_p4 , in_6, sub);
  // 一位进位加法器 一位进位加法器_8: pin names not known; wires that end beside it: \一位进位加法器_7_p5 , in_17, out_25, \一位进位加法器_8_p4 , sub
  xor xor_8 (\一位进位加法器_7_p4 , in_7, sub);
  xor xor_9 (\一位进位加法器_8_p4 , in_8, sub);
endmodule

// 全加器
module \一位进位加法器  (
  input  cin,
  input  a,
  input  b,
  output \进位 ,
  output \结果 
);

  wire and_1_out, and_2_out, and_3_out, xor_1_out;

  and and_1 (and_1_out, a, b);
  xor xor_1 (xor_1_out, a, b);
  and and_2 (and_2_out, cin, a);
  and and_3 (and_3_out, cin, b);
  or or_1 (\进位 , and_1_out, and_2_out, and_3_out);
  xor xor_2 (\结果 , cin, xor_1_out);
endmodule

module \八位可控加减器  (
  input  \sub控制位 ,
  input  a0,
  input  b0,
  input  a1,
  input  b1,
  input  a2,
  input  b2,
  input  a3,
  input  b3,
  input  a4,
  input  b4,
  input  a5,
  input  b5,
  input  a6,
  input  b6,
  input  a7,
  input  b7,
  output s0,
  output s1,
  output s2,
  output s3,
  output s4,
  output s5,
  output s6,
  output s7,
  output \溢出信号 ,
  output \进位信号 
);

  wire xor_1_out, xor_2_out, xor_3_out, xor_4_out, xor_5_out, xor_6_out, xor_7_out, xor_8_out,
       \一位进位加法器_1_p4 , \一位进位加法器_2_p5 , \一位进位加法器_3_p4 , \一位进位加法器_4_p4 , \一位进位加法器_5_p4 , \一位进位加法器_6_p4 ,
       \一位进位加法器_7_p4 ;

  xor xor_1 (xor_1_out, \sub控制位 , b0);
  xor xor_2 (xor_2_out, \sub控制位 , b1);
  xor xor_3 (xor_3_out, \sub控制位 , b2);
  xor xor_4 (xor_4_out, \sub控制位 , b3);
  xor xor_5 (xor_5_out, \sub控制位 , b4);
  xor xor_6 (xor_6_out, \sub控制位 , b5);
  xor xor_7 (xor_7_out, \sub控制位 , b6);
  xor xor_8 (xor_8_out, \sub控制位 , b7);
  // 一位进位加法器 一位进位加法器_1: pin names not known; wires that end beside it: a0, xor_1_out, \sub控制位 , \一位进位加法器_1_p4 , \一位进位加法器_1_p4 , s0
  // 一位进位加法器 一位进位加法器_2: pin names not known; wires that end beside it: a1, xor_2_out, \一位进位加法器_1_p4 , \一位进位加法器_1_p4 , \一位进位加法器_2_p5 , s1
  // 一位进位加法器 一位进位加法器_3: pin names not known; wires that end beside it: a2, xor_3_out, \一位进位加法器_2_p5 , \一位进位加法器_3_p4 , s2
  // 一位进位加法器 一位进位加法器_4: pin names not known; wires that end beside it: a3, xor_4_out, \一位进位加法器_3_p4 , \一位进位加法器_4_p4 , s3
  // 一位进位加法器 一位进位加法器_5: pin names not known; wires that end beside it: a4, xor_5_out, \一位进位加法器_4_p4 , \一位进位加法器_5_p4 , s4
  // 一位进位加法器 一位进位加法器_6: pin names not known; wires that end beside it: a5, xor_6_out, \一位进位加法器_5_p4 , \一位进位加法器_6_p4 , s5
  // 一位进位加法器 一位进位加法器_7: pin names not known; wires that end beside it: a6, xor_7_out, \一位进位加法器_6_p4 , \一位进位加法器_7_p4 , s6
  // 一位进位加法器 一位进位加法器_8: pin names not known; wires that end beside it: a7, xor_8_out, \一位进位加法器_7_p4 , \进位信号 , s7
  xor xor_9 (\溢出信号 , \一位进位加法器_7_p4 , \进位信号 );
endmodule
