// Logisim project logisim新手实验.circ as structural Verilog: 7 circuits, main circuit LED计数电路
module \LED计数电路  (
  input  in1,
  input  in2,
  input  in3,
  input  in4,
  input  in5,
  output out1,
  output out2,
  output out3,
  output out4,
  output out5
);

  or or_1 (out1, in1, in2, in3, in4, in5);
  or or_2 (out2, in2, in3, in4, in5);
  or or_3 (out3, in3, in4, in5);
  or or_4 (out4, in4, in5);

  assign out5 = in5;
endmodule

module \LED计数测试  (
);

  wire _1_out, _2_out, _3_out, _4_out, _5_out, \led计数电路_1_out1 , \led计数电路_1_out2 , \led计数电路_1_out3 ,
       \led计数电路_1_out4 , \led计数电路_1_out5 ;

  Button _1 (.out(_1_out));
  Button _2 (.out(_2_out));
  Button _3 (.out(_3_out));
  Button _4 (.out(_4_out));
  Button _5 (.out(_5_out));
  \LED计数电路  \led计数电路_1  (
    .in1(_1_out), .in2(_2_out), .in3(_3_out), .in4(_4_out), .in5(_5_out), .out1(\led计数电路_1_out1 ),
    .out2(\led计数电路_1_out2 ), .out3(\led计数电路_1_out3 ), .out4(\led计数电路_1_out4 ), .out5(\led计数电路_1_out5 ));
  LED led_1 (.in(\led计数电路_1_out1 ));
  LED led_2 (.in(\led计数电路_1_out2 ));
  LED led_3 (.in(\led计数电路_1_out3 ));
  LED led_4 (.in(\led计数电路_1_out4 ));
  LED led_5 (.in(\led计数电路_1_out5 ));
endmodule

module \_5输入按键编码器  (
  input  In1,
  input  In2,
  input  In3,
  input  In4,
  input  In5,
  output Out1,
  output Out2,
  output Out3
);

  wire and_1_out, and_2_out, and_3_out, and_4_out, not_1_out, not_2_out, not_3_out, not_4_out, not_5_out,
       not_6_out, not_7_out;

  not not_1 (not_1_out, In4);
  not not_2 (not_2_out, In2);
  not not_3 (not_3_out, In4);
  not not_4 (not_4_out, In4);
  not not_5 (not_5_out, In5);
  not not_6 (not_6_out, In4);
  not not_7 (not_7_out, In5);
  or or_1 (Out3, In5, In4);
  and and_1 (and_1_out, In3, not_1_out);
  and and_2 (and_2_out, In1, not_2_out, not_3_out);
  and and_3 (and_3_out, In3, not_4_out, not_5_out);
  and and_4 (and_4_out, In2, not_6_out, not_7_out);
  or or_2 (Out1, In5, and_1_out, and_2_out);
  or or_3 (Out2, and_3_out, and_4_out);
endmodule

module \_5输入编码电路测试  (
);

  wire _1_out, _2_out, _3_out, _4_out, _5_out, \led计数电路_1_out1 , \led计数电路_1_out2 , \led计数电路_1_out3 ,
       \led计数电路_1_out4 , \led计数电路_1_out5 ;
  wire [2:0] \n5输入按键编码器_1_out1 ;

  Button _1 (.out(_1_out));
  Button _2 (.out(_2_out));
  Button _3 (.out(_3_out));
  Button _4 (.out(_4_out));
  Button _5 (.out(_5_out));
  \LED计数电路  \led计数电路_1  (
    .in1(_1_out), .in2(_2_out), .in3(_3_out), .in4(_4_out), .in5(_5_out), .out1(\led计数电路_1_out1 ),
    .out2(\led计数电路_1_out2 ), .out3(\led计数电路_1_out3 ), .out4(\led计数电路_1_out4 ), .out5(\led计数电路_1_out5 ));
  \_5输入按键编码器  \u_5输入按键编码器_1  (
    .In1(_1_out), .In2(_2_out), .In3(_3_out), .In4(_4_out), .In5(_5_out), .Out1(\n5输入按键编码器_1_out1 [0]),
    .Out2(\n5输入按键编码器_1_out1 [1]), .Out3(\n5输入按键编码器_1_out1 [2]));
  // Probe on \n5输入按键编码器_1_out1 
  LED led_1 (.in(\led计数电路_1_out1 ));
  LED led_2 (.in(\led计数电路_1_out2 ));
  LED led_3 (.in(\led计数电路_1_out3 ));
  LED led_4 (.in(\led计数电路_1_out4 ));
  LED led_5 (.in(\led计数电路_1_out5 ));
  Hex_Digit_Display hex_digit_display_1 (.value({1'b0, \n5输入按键编码器_1_out1 }), .dp(1'b1));
endmodule

module \_7段数码管显示驱动  (
  input  X3,
  input  X2,
  input  X1,
  input  X0,
  output Seg_1,
  output Seg_2,
  output Seg_3,
  output Seg_4,
  output Seg_5,
  output Seg_6,
  output Seg_7
);

  wire and_1_out, and_2_out, and_3_out, and_4_out, and_5_out, and_6_out, and_7_out, and_8_out, and_9_out,
       and_10_out, and_11_out, and_12_out, and_13_out, and_14_out, and_15_out, and_16_out, not_1_out,
       not_2_out, not_3_out, not_4_out, not_5_out, not_6_out, not_7_out, not_8_out, not_9_out, not_10_out,
       not_11_out, not_12_out, not_13_out, not_14_out, not_15_out, not_16_out, not_17_out, not_18_out,
       not_19_out, not_20_out, not_21_out;

  not not_1 (not_1_out, X2);
  and and_1 (and_1_out, not_1_out, X1);
  and and_2 (and_2_out, X2, not_2_out);
  not not_2 (not_2_out, X1);
  and and_3 (and_3_out, X2, not_3_out);
  not not_3 (not_3_out, X0);
  not not_4 (not_4_out, X1);
  and and_4 (and_4_out, not_4_out, not_5_out);
  not not_5 (not_5_out, X0);
  and and_5 (and_5_out, X2, not_6_out);
  not not_6 (not_6_out, X1);
  and and_6 (and_6_out, X2, not_7_out);
  not not_7 (not_7_out, X0);
  not not_8 (not_8_out, X2);
  and and_7 (and_7_out, not_8_out, not_9_out);
  not not_9 (not_9_out, X0);
  and and_8 (and_8_out, X2, X0);
  not not_10 (not_10_out, X2);
  not not_11 (not_11_out, X1);
  and and_9 (and_9_out, not_11_out, not_12_out);
  not not_12 (not_12_out, X0);
  and and_10 (and_10_out, X1, X0);
  not not_13 (not_13_out, X2);
  and and_11 (and_11_out, not_13_out, not_14_out);
  not not_14 (not_14_out, X0);
  and and_12 (and_12_out, X1, not_15_out);
  not not_15 (not_15_out, X0);
  not not_16 (not_16_out, X2);
  and and_13 (and_13_out, not_16_out, not_17_out);
  not not_17 (not_17_out, X0);
  not not_18 (not_18_out, X2);
  and and_14 (and_14_out, not_18_out, X1);
  and and_15 (and_15_out, X1, not_19_out);
  not not_19 (not_19_out, X0);
  and and_16 (and_16_out, X2, not_20_out, X0);
  not not_20 (not_20_out, X1);
  not not_21 (not_21_out, X1);
  or or_1 (Seg_7, not_21_out, X0, X2);
  or or_2 (Seg_1, and_1_out, and_2_out, and_3_out, X3);
  or or_3 (Seg_2, and_4_out, and_5_out, and_6_out, X3);
  or or_4 (Seg_3, and_7_out, X1, and_8_out, X3);
  or or_5 (Seg_4, not_10_out, and_9_out, and_10_out);
  or or_6 (Seg_5, and_11_out, and_12_out);
  or or_7 (Seg_6, and_13_out, and_14_out, and_15_out, and_16_out);
endmodule

module \数码管驱动自动测试  (
);

  wire clock_1_out, \n7段数码管显示驱动_1_seg_1 , \n7段数码管显示驱动_1_seg_2 , \n7段数码管显示驱动_1_seg_3 , \n7段数码管显示驱动_1_seg_4 ,
       \n7段数码管显示驱动_1_seg_5 , \n7段数码管显示驱动_1_seg_6 , \n7段数码管显示驱动_1_seg_7 ;
  wire [3:0] counter_1_q;

  Clock clock_1 (.out(clock_1_out));
  Counter #(.width(4), .max('h5)) counter_1 (.Q(counter_1_q), .clk(clock_1_out));  // open: load, D, count, carry, clr
  \_7段数码管显示驱动  \u_7段数码管显示驱动_1  (
    .X3(counter_1_q[3]), .X2(counter_1_q[2]), .X1(counter_1_q[1]), .X0(counter_1_q[0]),
    .Seg_1(\n7段数码管显示驱动_1_seg_1 ), .Seg_2(\n7段数码管显示驱动_1_seg_2 ), .Seg_3(\n7段数码管显示驱动_1_seg_3 ),
    .Seg_4(\n7段数码管显示驱动_1_seg_4 ), .Seg_5(\n7段数码管显示驱动_1_seg_5 ), .Seg_6(\n7段数码管显示驱动_1_seg_6 ),
    .Seg_7(\n7段数码管显示驱动_1_seg_7 ));
  _7_Segment_Display u_7_segment_display_1 (
    .g(\n7段数码管显示驱动_1_seg_1 ), .f(\n7段数码管显示驱动_1_seg_2 ), .a(\n7段数码管显示驱动_1_seg_3 ), .b(\n7段数码管显示驱动_1_seg_4 ),
    .e(\n7段数码管显示驱动_1_seg_5 ), .d(\n7段数码管显示驱动_1_seg_6 ), .c(\n7段数码管显示驱动_1_seg_7 ));  // open: dp
endmodule

module \集成LED计数测试  (
);

  wire _1_out, _2_out, _3_out, _4_out, _5_out, \led计数电路_1_out1 , \led计数电路_1_out2 , \led计数电路_1_out3 ,
       \led计数电路_1_out4 , \led计数电路_1_out5 , \n7段数码管显示驱动_1_seg_1 , \n7段数码管显示驱动_1_seg_2 , \n7段数码管显示驱动_1_seg_3 ,
       \n7段数码管显示驱动_1_seg_4 , \n7段数码管显示驱动_1_seg_5 , \n7段数码管显示驱动_1_seg_6 , \n7段数码管显示驱动_1_seg_7 ;
  wire [2:0] \n5输入按键编码器_1_out1 ;

  Button _1 (.out(_1_out));
  Button _2 (.out(_2_out));
  Button _3 (.out(_3_out));
  Button _4 (.out(_4_out));
  Button _5 (.out(_5_out));
  \LED计数电路  \led计数电路_1  (
    .in1(_1_out), .in2(_2_out), .in3(_3_out), .in4(_4_out), .in5(_5_out), .out1(\led计数电路_1_out1 ),
    .out2(\led计数电路_1_out2 ), .out3(\led计数电路_1_out3 ), .out4(\led计数电路_1_out4 ), .out5(\led计数电路_1_out5 ));
  \_5输入按键编码器  \u_5输入按键编码器_1  (
    .In1(_1_out), .In2(_2_out), .In3(_3_out), .In4(_4_out), .In5(_5_out), .Out1(\n5输入按键编码器_1_out1 [0]),
    .Out2(\n5输入按键编码器_1_out1 [1]), .Out3(\n5输入按键编码器_1_out1 [2]));
  // Probe on \n5输入按键编码器_1_out1 
  LED led_1 (.in(\led计数电路_1_out1 ));
  LED led_2 (.in(\led计数电路_1_out2 ));
  LED led_3 (.in(\led计数电路_1_out3 ));
  LED led_4 (.in(\led计数电路_1_out4 ));
  LED led_5 (.in(\led计数电路_1_out5 ));
  \_7段数码管显示驱动  \u_7段数码管显示驱动_1  (
    .X3(1'b0), .X2(\n5输入按键编码器_1_out1 [2]), .X1(\n5输入按键编码器_1_out1 [1]), .X0(\n5输入按键编码器_1_out1 [0]),
    .Seg_1(\n7段数码管显示驱动_1_seg_1 ), .Seg_2(\n7段数码管显示驱动_1_seg_2 ), .Seg_3(\n7段数码管显示驱动_1_seg_3 ),
    .Seg_4(\n7段数码管显示驱动_1_seg_4 ), .Seg_5(\n7段数码管显示驱动_1_seg_5 ), .Seg_6(\n7段数码管显示驱动_1_seg_6 ),
    .Seg_7(\n7段数码管显示驱动_1_seg_7 ));
  Hex_Digit_Display hex_digit_display_1 (.value({1'b0, \n5输入按键编码器_1_out1 }), .dp(1'b1));
  _7_Segment_Display u_7_segment_display_1 (
    .g(\n7段数码管显示驱动_1_seg_1 ), .f(\n7段数码管显示驱动_1_seg_2 ), .a(\n7段数码管显示驱动_1_seg_3 ), .b(\n7段数码管显示驱动_1_seg_4 ),
    .e(\n7段数码管显示驱动_1_seg_5 ), .d(\n7段数码管显示驱动_1_seg_6 ), .c(\n7段数码管显示驱动_1_seg_7 ), .dp(1'b1));
endmodule
